# Fritzing sketch UARTPOT (saved by Fritzing 0.9.4)

parts:
  M1 = STM32407VG Discovery
  Part1 = XBee USB Mini Adapter
  R1 = TRIMPOT [package=3386u]

nets:
  N1: M1.GND-13, M1.GND-24, M1.GND-99, Part1.GND, R1.CCW
  N2: M1.PA3, Part1.TXD
  N3: M1.PA2, Part1.RXD
  N4: M1.PA0, R1.WIPER
  N5: M1.3V-97, M1.3V-101, R1.CW

custom parts:
  STM32407VG Discovery: The STM32F4DISCOVERY Discovery kit allows users to easily develop applications with the STM32F407VG high performance microcontroller with the ARM® Cortex®-M4 32-bit core. It includes everything required either for beginners or for experienced users to get quickly started.Based on STM32F407VG, it includes an ST-LINK/V2 or ST-LINK/V2-A embedded debug tool, two ST-MEMS digital accelerometers, a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
